// Logisim project lab1.circ as structural Verilog
module sort (
  input  [3:0] x0,
  input  [3:0] x1,
  input  [3:0] x2,
  input  [3:0] x3,
  input  rst,
  input  [2:0] FSM
);

  wire ALU_y_cf_zf_sf_of_of, ALU_y_cf_zf_sf_of_sf, ALU_y_cf_zf_sf_of_zf, and_1_out, and_2_out, and_3_out,
       and_4_out, and_5_out, clk_out, decoder_1_out1, decoder_1_out2, decoder_1_out3, decoder_1_out4,
       decoder_1_out5, decoder_1_out6, not_1_out, or_1_out, or_2_out, or_3_out, or_4_out, or_5_out,
       xnor_1_out;
  wire [3:0] multiplexer_1_out, multiplexer_2_out, multiplexer_3_out, multiplexer_4_out, multiplexer_5_out,
       multiplexer_6_out, R0_q, R1_q, R2_q, R3_q;

  Clock clk (.out(clk_out));
  Multiplexer #(.width(4), .enable("false")) multiplexer_1 (
    .in0(x0), .in1(R1_q), .out(multiplexer_1_out), .sel(and_5_out));
  Multiplexer #(.width(4), .enable("false")) multiplexer_2 (
    .in0(x1), .in1(multiplexer_5_out), .out(multiplexer_2_out), .sel(and_5_out));
  Multiplexer #(.width(4), .enable("false")) multiplexer_3 (
    .in0(x2), .in1(multiplexer_6_out), .out(multiplexer_3_out), .sel(and_5_out));
  Multiplexer #(.width(4), .enable("false")) multiplexer_4 (
    .in0(x3), .in1(R2_q), .out(multiplexer_4_out), .sel(and_5_out));
  and and_1 (and_1_out, or_4_out, and_5_out);
  or or_1 (or_1_out, or_4_out, or_5_out);
  or or_2 (or_2_out, or_5_out, decoder_1_out3);
  and and_2 (and_2_out, decoder_1_out3, and_5_out);
  and and_3 (and_3_out, or_1_out, and_5_out);
  and and_4 (and_4_out, or_2_out, and_5_out);
  Register #(.width(4)) R0 (.D(multiplexer_1_out), .en(and_1_out), .Q(R0_q), .clk(clk_out), .clr(rst));
  Register #(.width(4)) R1 (.D(multiplexer_2_out), .en(and_3_out), .Q(R1_q), .clk(clk_out), .clr(rst));
  Register #(.width(4)) R2 (.D(multiplexer_3_out), .en(and_4_out), .Q(R2_q), .clk(clk_out), .clr(rst));
  Register #(.width(4)) R3 (.D(multiplexer_4_out), .en(and_2_out), .Q(R3_q), .clk(clk_out), .clr(rst));
  or or_3 (or_3_out, decoder_1_out3, or_5_out);
  Multiplexer #(.width(4), .enable("false")) multiplexer_5 (
    .in0(R0_q), .in1(R2_q), .out(multiplexer_5_out), .sel(or_3_out));
  Multiplexer #(.width(4), .enable("false")) multiplexer_6 (
    .in0(R1_q), .in1(R3_q), .out(multiplexer_6_out), .sel(decoder_1_out3));
  or or_4 (or_4_out, decoder_1_out1, decoder_1_out4, decoder_1_out6);
  Decoder #(.select(3), .enable("false")) decoder_1 (
    .out1(decoder_1_out1), .out2(decoder_1_out2), .out3(decoder_1_out3), .out4(decoder_1_out4),
    .out5(decoder_1_out5), .out6(decoder_1_out6), .sel(FSM));  // open: out0, out7
  ALU ALU_y_cf_zf_sf_of (
    .a(multiplexer_5_out), .b(multiplexer_6_out), .zf(ALU_y_cf_zf_sf_of_zf), .sf(ALU_y_cf_zf_sf_of_sf),
    .of(ALU_y_cf_zf_sf_of_of));  // open: y, cf
  or or_5 (or_5_out, decoder_1_out2, decoder_1_out5);
  not not_1 (not_1_out, ALU_y_cf_zf_sf_of_zf);
  and and_5 (and_5_out, not_1_out, xnor_1_out);
  xnor xnor_1 (xnor_1_out, ALU_y_cf_zf_sf_of_sf, ALU_y_cf_zf_sf_of_of);

  // Notes on the sheet:
  //   M0
  //   M1
  //   M2
  //   M3
  //   注：M0-M3在实现时控制信号来源于FSM而非ALU，我认为从ALU引出来也可以，详见summary
  //   M4
  //   M5
  //   PB18000227艾语晨
endmodule

module ALU (
  input  [3:0] a,
  input  [3:0] b,
  output [3:0] y,
  output cf,
  output zf,
  output sf,
  output of
);

  wire and_1_out, and_2_out, not_1_out, not_2_out, not_3_out;

  Subtractor #(.width(4)) subtractor_1 (.a(a), .b(b), .out({sf, y[2:0]}), .bout(cf));  // open: bin
  not not_1 (not_1_out, b[3]);
  not not_2 (not_2_out, a[3]);
  not not_3 (not_3_out, sf);
  and and_1 (and_1_out, not_2_out, b[3], sf);
  nor nor_1 (zf, y[0], y[1], y[2], sf);
  and and_2 (and_2_out, a[3], not_1_out, not_3_out);
  or or_1 (of, and_2_out, and_1_out);

  assign y[3] = sf;

  // Notes on the sheet:
  //   PB18000227艾语晨
endmodule
